# Fritzing sketch randomLEDs (saved by Fritzing 0.9.10b)
breadboards: 1

parts:
  Part1 = Arduino Uno (Rev3)
  LED1 = LED - 5mm [color="Green (555nm)" current=0.030 package="5 mm [THT]"]
  LED2 = LED - 5mm [color="Red (633nm)" current=0.030 package="5 mm [THT]"]
  LED3 = LED - 5mm [color="Green (555nm)" current=0.030 package="5 mm [THT]"]
  LED4 = LED - 5mm [color="Red (633nm)" current=0.030 package="5 mm [THT]"]
  LED5 = LED - 5mm [color="Red (633nm)" current=0.030 package="5 mm [THT]"]
  LED6 = LED - 5mm [color="Green (555nm)" current=0.030 package="5 mm [THT]"]
  LED7 = LED - 5mm [color="Red (633nm)" current=0.030 package="5 mm [THT]"]
  LED8 = LED - 5mm [color="Green (555nm)" current=0.030 package="5 mm [THT]"]
  R2 = Resistor [tolerance=±5% power=0.25 resistance=220 package=THT]
  R3 = Resistor [tolerance=±5% power=0.25 resistance=220 package=THT]
  R4 = Resistor [tolerance=±5% power=0.25 resistance=220 package=THT]
  R5 = Resistor [tolerance=±5% power=0.25 resistance=220 package=THT]
  R6 = Resistor [tolerance=±5% power=0.25 resistance=220 package=THT]
  R7 = Resistor [tolerance=±5% power=0.25 resistance=220 package=THT]
  R8 = Resistor [tolerance=±5% power=0.25 resistance=220 package=THT]
  R9 = Resistor [tolerance=±5% power=0.25 resistance=220 package=THT]

nets:
  N1: Part1.D8, LED2.anode
  N2: Part1.D9_PWM, LED1.anode
  N3: Part1.D10_PWM/SS, LED8.anode
  N4: Part1.D11_PWM/MOSI, LED7.anode
  N5: Part1.D12/MISO, LED6.anode
  N6: Part1.D13/SCK, LED5.anode
  N7: Part1.D6_PWM, LED4.anode
  N8: Part1.D7, LED3.anode
  N9: Part1.GND, R2.Pin_1, R3.Pin_1, R4.Pin_1, R5.Pin_1, R6.Pin_0, R7.Pin_0, R8.Pin_0, R9.Pin_0
  N10: LED1.cathode, R8.Pin_1
  N11: LED2.cathode, R9.Pin_1
  N12: LED3.cathode, R6.Pin_1
  N13: LED4.cathode, R7.Pin_1
  N14: LED5.cathode, R2.Pin_0
  N15: LED6.cathode, R3.Pin_0
  N16: LED7.cathode, R4.Pin_0
  N17: LED8.cathode, R5.Pin_0
